# Fritzing sketch countdown (saved by Fritzing 0.9.3b)
circuit board: 0.6cm x 0.6cm
circuit board: 0.6cm x 0.6cm
circuit board: 0.6cm x 0.6cm
circuit board: 2.25cm x 3.29cm
circuit board: 2.25cm x 3.29cm
breadboards: 1

parts:
  U3 = IC, SIP package, 5 pins [chip_label=IC]
  U2 = IC, SIP package, 5 pins [chip_label=IC]
  U4 = SO16 [chip_label=TLC5916 package=SO]
  U6 = IC, SIP package, 7 pins [chip_label=IC]
  U5 = IC, SIP package, 7 pins [chip_label=IC]
  U7 = SO16 [chip_label=TLC5916 package=SO]
  J1 = double row female pin header, 8 pins [form="♀ (female)"]  # not connected
  J2 = female pin header, 8 pins [form="♀ (female)"]
  J3 = female pin header, 8 pins [form="♀ (female)"]

nets:
  N1: U3.pin1, U7.10
  N2: U3.pin2, U7.9
  N3: U3.pin3, J2.pin8, J3.pin8
  N4: U3.pin4, U7.8
  N5: U3.pin5, U7.7
  N6: U2.pin1, U7.6
  N7: U2.pin2, U7.5
  N8: U2.pin4, U7.12
  N9: U2.pin5, U7.11
  N10: U4.5, U6.pin6
  N11: U4.6, U6.pin4
  N12: U4.7, U6.pin3
  N13: U4.9, U6.pin1
  N14: U4.10, U5.pin7
  N15: U4.11, U5.pin2
  N16: U4.12, U5.pin1
  N17: U7.1, J2.pin2, J3.pin2
  N18: U7.2, J2.pin3
  N19: U7.3, J2.pin4, J3.pin4
  N20: U7.4, J2.pin5, J3.pin5
  N21: U7.13, J2.pin6, J3.pin6
  N22: U7.14, J3.pin3
  N23: U7.16, J2.pin1, J3.pin1
